# Fritzing sketch garage (saved by Fritzing 0.9.2b)
perfboards: 1

parts:
  Part1 = Arduino Pro Mini v13
  DIP-Relay1 = DIP-Relay-D31A [part_number=D31A*]
  J1 = Screw terminal - 2 pins [package=THT]
  Q1 = NPN-Transistor [package="TO92 [THT]"]
  C1 = Ceramic Capacitor [capacitance=100nF package="100 mil [THT, multilayer]"]
  D1 = Rectifier Diode [part_number=1N4001 package="300 mil [THT]"]
  J2 = Screw terminal - 2 pins [package=THT]
  S1 = Pushbutton [package="[THT]"]
  R1 = Resistor [tolerance=±5% resistance=220 package=THT]

nets:
  N1: Part1.D8, J1.pin1, Q1.E, R1.Pin_0
  N2: Part1.D6_PWM, DIP-Relay1.B1_Switch_Terminal_B, J1.pin2, D1.cathode
  N3: Part1.D4, C1.1
  N4: Part1.D2, R1.Pin_1
  N5: DIP-Relay1.A1_Switch_Terminal_A, J2.pin2
  N6: DIP-Relay1.COIL1_+, J2.pin1
  N7: DIP-Relay1.B2_Switch_Terminal_B, Q1.C, D1.anode
  N8: Q1.B, C1.0
  N9: S1.Pin_1, S1.Pin_2
  N10: S1.Pin_3, S1.Pin_4
